// Logisim project LAOCprocessador.circ as structural Verilog: 5 circuits, main circuit main
module main (
  input  in_1
);

  wire ALUSrc, and_1_out, Branch, clock_1_out, Jump, MemRead, MemToReg, MemWrite, not_1_out, or_1_out,
       RegDst, RegWrite, ULA_igual;
  wire [1:0] ALUOp;
  wire [2:0] controle_da_ula_1_ulactrl, multiplexer_2_out, opcode, rs, rt;
  wire [2:2] rd;
  wire [7:0] adder_1_out, address_imm, Bando_de_Registradores_read_data_1, Cont_rt, multiplexer_1_out,
       multiplexer_3_out, multiplexer_4_out, PC_q, ram_1_data, ULA_r;

  Clock clock_1 (.out(clock_1_out));
  Register PC (.D(multiplexer_1_out), .Q(PC_q), .clk(clock_1_out), .clr(in_1));  // open: en
  Adder adder_1 (.a(8'h1), .b(PC_q), .out(adder_1_out));  // open: cin, cout
  Multiplexer #(.width(8), .enable("false")) multiplexer_1 (
    .in0(adder_1_out), .in1(address_imm), .out(multiplexer_1_out), .sel(or_1_out));
  ROM #(.dataWidth(18)) rom_1 (.addr(PC_q), .data({opcode, rs, rt, rd[2], address_imm}));  // open: sel
  Multiplexer #(.width(3), .enable("false")) multiplexer_2 (
    .in0(rt), .in1({rd[2], address_imm[7:6]}), .out(multiplexer_2_out), .sel(RegDst));
  Unidade_de_Controle Unidade_de_Controle (
    .opcode(opcode), .RegDst(RegDst), .RegWrite(RegWrite), .ALUSrc(ALUSrc), .MemWrite(MemWrite),
    .MemRead(MemRead), .MemToReg(MemToReg), .Branch(Branch), .Jump(Jump), .ALUOp(ALUOp));
  Banco_de_Registradores Bando_de_Registradores (
    .Read_Register_1(rs), .Read_Register2(rt), .Write_Data(multiplexer_4_out),
    .Write_Register(multiplexer_2_out), .Reg_Write(RegWrite), .Clock(clock_1_out), .Clear(in_1),
    .Read_Data_1(Bando_de_Registradores_read_data_1), .Read_Data_2(Cont_rt));
  ULA ULA (
    .A(Bando_de_Registradores_read_data_1), .B(multiplexer_3_out), .\Função (controle_da_ula_1_ulactrl),
    .Shamt(address_imm[5:3]), .R(ULA_r), .igual(ULA_igual));
  Multiplexer #(.width(8), .enable("false")) multiplexer_3 (
    .in0(Cont_rt), .in1(address_imm), .out(multiplexer_3_out), .sel(ALUSrc));
  Controle_da_ULA controle_da_ula_1 (.Funct(address_imm[2:0]), .ALUOp(ALUOp), .ULACtrl(controle_da_ula_1_ulactrl));
  or or_1 (or_1_out, and_1_out, Jump);
  and and_1 (and_1_out, ULA_igual, Branch);
  not not_1 (not_1_out, clock_1_out);
  Multiplexer #(.width(8), .enable("false")) multiplexer_4 (
    .in0(ULA_r), .in1(ram_1_data), .out(multiplexer_4_out), .sel(MemToReg));
  RAM #(.bus("separate")) ram_1 (
    .addr(ULA_r), .din(Cont_rt), .data(ram_1_data), .str(MemWrite), .clk(not_1_out), .ld(MemRead), .clr(in_1));  // open: sel

  // Other names for the same wires on the sheet: funct[2:0] = address_imm[2:0]; rd[1:0] = address_imm[7:6];
  //   shamt[2:0] = address_imm[5:3]

  // Notes on the sheet:
  //   contents of rom_1 (hex, n*v repeats v):
  //   20a08 10a00 20e08 20203 17200 20205 17201 20204 17202 20201 17203 20207 17204 20207 17205 20208
  //   17206 20205 17207 20c00 20800 4a45 1901d 7840 9200 6380 24801 38016 6b83 10c01
endmodule

module Banco_de_Registradores (
  input  [2:0] Read_Register_1,
  input  [2:0] Read_Register2,
  input  [7:0] Write_Data,
  input  [2:0] Write_Register,
  input  Reg_Write,
  input  Clock,
  input  Clear,
  output [7:0] Read_Data_1,
  output [7:0] Read_Data_2
);

  wire WE0, WE1, WE2, WE3, WE4, WE5, WE6, WE7;
  wire [7:0] demultiplexer_2_out0, demultiplexer_2_out1, demultiplexer_2_out2, demultiplexer_2_out3,
       demultiplexer_2_out4, demultiplexer_2_out5, demultiplexer_2_out6, demultiplexer_2_out7, Reg0, Reg1,
       Reg2, Reg3, Reg4, Reg5, Reg6, Reg7;

  Demultiplexer #(.select(3), .enable("false")) demultiplexer_1 (
    .out0(WE0), .out1(WE1), .out2(WE2), .out3(WE3), .out4(WE4), .out5(WE5), .out6(WE6), .out7(WE7),
    .in(Reg_Write), .sel(Write_Register));
  Demultiplexer #(.select(3), .width(8), .enable("false")) demultiplexer_2 (
    .out0(demultiplexer_2_out0), .out1(demultiplexer_2_out1), .out2(demultiplexer_2_out2),
    .out3(demultiplexer_2_out3), .out4(demultiplexer_2_out4), .out5(demultiplexer_2_out5),
    .out6(demultiplexer_2_out6), .out7(demultiplexer_2_out7), .in(Write_Data), .sel(Write_Register));
  Register u_Reg0 (.D(demultiplexer_2_out0), .en(WE0), .Q(Reg0), .clk(Clock), .clr(Clear));
  Register u_Reg1 (.D(demultiplexer_2_out1), .en(WE1), .Q(Reg1), .clk(Clock), .clr(Clear));
  Register u_Reg2 (.D(demultiplexer_2_out2), .en(WE2), .Q(Reg2), .clk(Clock), .clr(Clear));
  Register u_Reg3 (.D(demultiplexer_2_out3), .en(WE3), .Q(Reg3), .clk(Clock), .clr(Clear));
  Register u_Reg4 (.D(demultiplexer_2_out4), .en(WE4), .Q(Reg4), .clk(Clock), .clr(Clear));
  Register u_Reg5 (.D(demultiplexer_2_out5), .en(WE5), .Q(Reg5), .clk(Clock), .clr(Clear));
  Register u_Reg6 (.D(demultiplexer_2_out6), .en(WE6), .Q(Reg6), .clk(Clock), .clr(Clear));
  Register u_Reg7 (.D(demultiplexer_2_out7), .en(WE7), .Q(Reg7), .clk(Clock), .clr(Clear));
  Multiplexer #(.select(3), .width(8), .enable("false")) multiplexer_1 (
    .in0(Reg0), .in1(Reg1), .in2(Reg2), .in3(Reg3), .in4(Reg4), .in5(Reg5), .in6(Reg6), .in7(Reg7),
    .out(Read_Data_1), .sel(Read_Register_1));
  Multiplexer #(.select(3), .width(8), .enable("false")) multiplexer_2 (
    .in0(Reg0), .in1(Reg1), .in2(Reg2), .in3(Reg3), .in4(Reg4), .in5(Reg5), .in6(Reg6), .in7(Reg7),
    .out(Read_Data_2), .sel(Read_Register2));

  // Other names for the same wires on the sheet: Read1[2:0] = Read_Register_1; Read2[2:0] = Read_Register2
endmodule

module Unidade_de_Controle (
  input  [2:0] opcode,
  output RegDst,
  output RegWrite,
  output ALUSrc,
  output MemWrite,
  output MemRead,
  output MemToReg,
  output Branch,
  output Jump,
  output [1:0] ALUOp
);

  wire and_1_out, and_7_out, and_8_out, nor_2_out;

  nor nor_1 (RegDst, opcode[0], opcode[1], opcode[2]);
  nor nor_2 (nor_2_out, opcode[1], opcode[2]);
  or or_1 (RegWrite, nor_2_out, and_1_out);
  and and_1 (and_1_out, ~opcode[0], ~opcode[1], opcode[2]);  // AND_Gate
  ExactlyOne xor_1 (.out(ALUSrc), .in0(opcode[0]), .in1(opcode[1]), .in2(opcode[2]));
  and and_2 (MemWrite, ~opcode[0], opcode[1], ~opcode[2]);  // AND_Gate
  and and_3 (MemRead, opcode[0], ~opcode[1], ~opcode[2]);  // AND_Gate
  and and_4 (MemToReg, opcode[0], ~opcode[1], ~opcode[2]);  // AND_Gate
  and and_5 (Branch, opcode[0], opcode[1], ~opcode[2]);  // AND_Gate
  and and_6 (Jump, opcode[0], opcode[1], opcode[2]);
  and and_7 (and_7_out, opcode[0], opcode[1], ~opcode[2]);  // AND_Gate
  or or_2 (ALUOp[0], and_7_out, and_8_out);
  and and_8 (and_8_out, ~opcode[0], ~opcode[1], opcode[2]);  // AND_Gate
  and and_9 (ALUOp[1], ~opcode[0], ~opcode[1]);  // AND_Gate
endmodule

module Controle_da_ULA (
  input  [2:0] Funct,
  input  [1:0] ALUOp,
  output [2:0] ULACtrl
);

  Multiplexer #(.select(2), .width(3), .enable("false")) multiplexer_1 (
    .in0(3'b000), .in1(3'b101), .in2(Funct), .in3(3'b000), .out(ULACtrl), .sel(ALUOp));
endmodule

module ULA (
  input  [7:0] A,
  input  [7:0] B,
  input  [2:0] \Função ,
  input  [2:0] Shamt,
  output [7:0] R,
  output igual
);

  wire comparator_1_lt;
  wire [7:0] AComp, adder_1_out, ADiv, AMult, ANeg, AShiftDir, AShiftEsq, ASoma, ASub, BComp, BDiv,
       bit_extender_1_out, BMult, BSoma, BSub, divider_1_out, multiplier_1_out, negator_1_out, shifter_1_out,
       subtractor_1_out;

  Demultiplexer #(.select(3), .width(8), .enable("false")) demultiplexer_1 (
    .out0(ASoma), .out1(ASub), .out2(AMult), .out3(ADiv), .out4(ANeg), .out5(AComp), .out6(AShiftEsq),
    .out7(AShiftDir), .in(A), .sel(\Função ));
  Demultiplexer #(.select(3), .width(8), .enable("false")) demultiplexer_2 (
    .out0(BSoma), .out1(BSub), .out2(BMult), .out3(BDiv), .out5(BComp), .in(B), .sel(\Função ));  // open: out4, out6, out7
  Adder adder_1 (.a(ASoma), .b(BSoma), .out(adder_1_out));  // open: cin, cout
  Subtractor subtractor_1 (.a(ASub), .b(BSub), .out(subtractor_1_out));  // open: bin, bout
  Multiplier multiplier_1 (.a(AMult), .b(BMult), .out(multiplier_1_out));  // open: cin, cout
  Divider divider_1 (.a(ADiv), .b(BDiv), .out(divider_1_out));  // open: upper, rem
  Negator negator_1 (.in(ANeg), .out(negator_1_out));
  Comparator comparator_1 (.a(AComp), .b(BComp), .eq(igual), .lt(comparator_1_lt));  // open: gt
  Shifter shifter_1 (.in(AShiftDir), .\dist (Shamt), .out(shifter_1_out));
  Shifter #(.shift("lr")) shifter_2 (.in(AShiftDir), .\dist (Shamt), .out(shifter_1_out));
  assign bit_extender_1_out = {{7{1'b0}}, comparator_1_lt};  // Bit_Extender bit_extender_1
  Multiplexer #(.select(3), .width(8), .enable("false")) multiplexer_1 (
    .in0(adder_1_out), .in1(subtractor_1_out), .in2(multiplier_1_out), .in3(divider_1_out),
    .in4(negator_1_out), .in5(bit_extender_1_out), .in6(shifter_1_out), .in7(shifter_1_out), .out(R),
    .sel(\Função ));
endmodule
